// Logisim project cpu.circ as structural Verilog: 3 circuits, main circuit main
module main (
  input  [31:0] INSTRUCTION,
  input  CLOCK,
  output [31:0] PROGRAM_COUNTER,
  output [31:0] ra,
  output [31:0] sp,
  output [31:0] t0,
  output [31:0] t1,
  output [31:0] t2,
  output [31:0] s0,
  output [31:0] s1,
  output [31:0] a0
);

  wire and_1_out, BrEq, BrLT, BrUn, BSel, comparator_1_eq, comparator_1_lt, comparator_2_eq, comparator_2_lt,
       comparator_3_eq, comparator_4_eq, comparator_5_eq, MemRW, PCSel, RegWEn, reset, undriven, undriven_2;
  wire [1:0] ASel, WBSel;
  wire [2:0] ImmSel;
  wire [3:0] ALUSel;
  wire [4:0] addr1, addr2;
  wire [31:0] adder_1_out, adder_2_out, ALU_res, Imm, INSTRUCTION_EX, INSTRUCTION_REG, Mem,
       multiplexer_1_out, multiplexer_4_out, multiplexer_5_out, PROGRAM_COUNTER_EX, rs1, rs2, wb;

  Adder #(.width(32)) adder_1 (.a(PROGRAM_COUNTER), .b(32'h4), .out(adder_1_out));  // open: cin, cout
  Multiplexer #(.width(32), .enable("false")) multiplexer_1 (
    .in0(adder_1_out), .in1(ALU_res), .out(multiplexer_1_out), .sel(PCSel));
  Register #(.width(32)) PC (.D(multiplexer_1_out), .clk(CLOCK), .Q(PROGRAM_COUNTER));  // open: en, clr
  Control control_1 (
    .instruction({INSTRUCTION_EX[31:25], addr2, addr1, INSTRUCTION_EX[14:0]}), .BrEq(BrEq), .BrLT(BrLT),
    .PCSel(PCSel), .ImmSel(ImmSel), .BrUn(BrUn), .ASel(ASel), .BSel(BSel), .ALUSel(ALUSel), .MemRW(MemRW),
    .RegWEn(RegWEn), .WBSel(WBSel));
  ImmGen immgen_1 (
    .instruction({INSTRUCTION_EX[31:25], addr2, addr1, INSTRUCTION_EX[14:0]}), .ImmSel(ImmSel), .Imm(Imm));
  regfile_main RegFile (
    .rs2(addr2), .rd(INSTRUCTION_EX[11:7]), .Read_Data_1(rs1), .Read_Data_2(rs2), .ra(ra), .sp(sp), .t0(t0),
    .t1(t1), .t2(t2), .s0(s0), .s1(s1), .a0(a0), .rs1(addr1), .Write_Data(wb), .RegWEn(RegWEn), .clk(CLOCK));
  Comparator #(.width(32)) comparator_1 (.a(rs1), .b(rs2), .eq(comparator_1_eq), .lt(comparator_1_lt));  // open: gt
  Comparator #(.width(32), .mode("unsigned")) comparator_2 (
    .a(rs1), .b(rs2), .eq(comparator_2_eq), .lt(comparator_2_lt));  // open: gt
  Register #(.width(32)) register_1 (
    .D(INSTRUCTION_REG), .en(undriven), .clk(CLOCK),
    .Q({INSTRUCTION_EX[31:25], addr2, addr1, INSTRUCTION_EX[14:0]}));  // open: clr
  Register #(.width(32)) register_2 (
    .D(PROGRAM_COUNTER), .en(undriven_2), .clk(CLOCK), .Q(PROGRAM_COUNTER_EX));  // open: clr
  Multiplexer #(.enable("false")) multiplexer_2 (.in0(comparator_1_eq), .in1(comparator_2_eq), .out(BrEq), .sel(BrUn));
  Multiplexer #(.enable("false")) multiplexer_3 (.in0(comparator_1_lt), .in1(comparator_2_lt), .out(BrLT), .sel(BrUn));
  Multiplexer #(.select(2), .width(32), .enable("false")) multiplexer_4 (
    .in0(rs1), .in1(PROGRAM_COUNTER_EX), .in2({32{1'b0}}), .out(multiplexer_4_out), .sel(ASel));  // open: in3
  Multiplexer #(.width(32), .enable("false")) multiplexer_5 (.in0(rs2), .in1(Imm), .out(multiplexer_5_out), .sel(BSel));
  Comparator #(.width(7)) comparator_3 (.a(INSTRUCTION_EX[6:0]), .b(7'b1100011), .eq(comparator_3_eq));  // open: gt, lt
  alu Arithmetic_Logic_Unit (.ALUSel(ALUSel), .B(multiplexer_5_out), .A(multiplexer_4_out), .Result(ALU_res));
  Multiplexer #(.width(32), .enable("false")) multiplexer_6 (
    .in0(INSTRUCTION), .in1(32'h13), .out(INSTRUCTION_REG), .sel(reset));
  and and_1 (and_1_out, comparator_3_eq, PCSel);
  Adder #(.width(32)) adder_2 (.a(PROGRAM_COUNTER_EX), .b(32'h4), .out(adder_2_out));  // open: cin, cout
  Comparator #(.width(7)) comparator_4 (.a(INSTRUCTION_EX[6:0]), .b(7'b1100111), .eq(comparator_4_eq));  // open: gt, lt
  Comparator #(.width(7)) comparator_5 (.a(INSTRUCTION_EX[6:0]), .b(7'b1101111), .eq(comparator_5_eq));  // open: gt, lt
  or or_1 (reset, and_1_out, comparator_4_eq, comparator_5_eq);
  Multiplexer #(.select(2), .width(32), .enable("false")) multiplexer_7 (
    .in0(ALU_res), .in1(adder_2_out), .in2(Mem), .out(wb), .sel(WBSel));  // open: in3
  // mem_main DMEM: pin names not known; wires that end beside it: ALU_res, rs2, CLOCK, MemRW, Mem

  // Other names for the same wires on the sheet: clk = CLOCK; Opcode[6:0] = INSTRUCTION_EX[6:0];
  //   rd[4:0] = INSTRUCTION_EX[11:7]; INSTRUCTION_EX[24:15] = {addr2, addr1}

  // Notes on the sheet:
  //   Output
  //   IMEM (do **NOT** move this)
  //   Inputs
  //   It is OK to move the PC, RegFile, ALU, and MEM to wherever is most convenient for you when constructing your CPU, and to delete this text
  //   Inputs/Outputs for testing. Do **NOT** move these.
endmodule

module ImmGen (
  input  [31:0] instruction,
  input  [2:0] ImmSel,
  output [31:0] Imm
);

  wire [31:0] B, I, J, S;

  Multiplexer #(.select(3), .width(32), .enable("false")) multiplexer_1 (
    .in0(I), .in1(S), .in2(B), .in3({instruction[31:12], {12{1'b0}}}), .in4(J), .out(Imm), .sel(ImmSel));  // open: in5, in6, in7
  assign I = {{20{instruction[31]}}, instruction[31:20]};  // Bit_Extender bit_extender_1
  assign S = {{20{instruction[31]}}, {instruction[31:25], instruction[11:7]}};  // Bit_Extender bit_extender_2
  assign B = {{19{instruction[31]}}, {instruction[31], instruction[7], instruction[30:25], instruction[11:8], 1'b0}};  // Bit_Extender bit_extender_3
  assign J = {{11{instruction[31]}}, {instruction[31], instruction[20:12], instruction[30:21], 1'b0}};  // Bit_Extender bit_extender_4

  // Other names for the same wires on the sheet: U[31:12] = instruction[31:12]
endmodule

module Control (
  input  [31:0] instruction,
  input  BrEq,
  input  BrLT,
  output PCSel,
  output [2:0] ImmSel,
  output BrUn,
  output [1:0] ASel,
  output BSel,
  output [3:0] ALUSel,
  output MemRW,
  output RegWEn,
  output [1:0] WBSel
);

  wire and_1_out, and_2_out, and_3_out, and_4_out, and_5_out, ASel_PC, comparator_1_eq, comparator_2_eq,
       comparator_3_eq, comparator_4_eq, comparator_5_eq, comparator_7_eq, comparator_8_eq, comparator_9_eq,
       comparator_10_eq, comparator_11_eq, comparator_12_eq, comparator_13_eq, comparator_14_eq,
       comparator_15_eq, comparator_16_eq, not_1_out, or_1_out, or_4_out, or_5_out;
  wire [1:0] multiplexer_2_out;
  wire [3:0] funct, I_ALU, multiplexer_8_out, R_ALU;

  not not_1 (not_1_out, BrEq);
  Comparator #(.width(7)) comparator_1 (.a(instruction[6:0]), .b(7'b1100011), .eq(comparator_1_eq));  // open: gt, lt
  Comparator #(.width(3)) comparator_2 (.a(instruction[14:12]), .b(3'b000), .eq(comparator_2_eq));  // open: gt, lt
  Comparator #(.width(3)) comparator_3 (.a(instruction[14:12]), .b(3'b001), .eq(comparator_3_eq));  // open: gt, lt
  Comparator #(.width(3)) comparator_4 (.a(instruction[14:12]), .b(3'b100), .eq(comparator_4_eq));  // open: gt, lt
  Comparator #(.width(3)) comparator_5 (.a(instruction[14:12]), .b(3'b110), .eq(comparator_5_eq));  // open: gt, lt
  Comparator #(.width(7)) comparator_6 (.a(instruction[6:0]), .b(7'b0100011), .eq(MemRW));  // open: gt, lt
  and and_1 (and_1_out, comparator_2_eq, BrEq);
  and and_2 (and_2_out, comparator_3_eq, not_1_out);
  and and_3 (and_3_out, comparator_4_eq, BrLT);
  and and_4 (and_4_out, comparator_5_eq, BrLT);
  Multiplexer #(.select(5), .width(3), .enable("false")) multiplexer_1 (
    .in0(3'b000), .in4(3'b000), .in8(3'b001), .in13(3'b011), .in24(3'b010), .in25(3'b000), .in27(3'b100),
    .out(ImmSel), .sel(instruction[6:2]));  // open: in1, in2, in3, in5, in6, in7, in9, in10, in11, in12, in14, in15, in16, in17, in18, in19, in20, in21, in22, in23, in26, in28, in29, in30, in31
  or or_1 (or_1_out, and_1_out, and_2_out, and_3_out, and_4_out);
  and and_5 (and_5_out, comparator_1_eq, or_1_out);
  Comparator #(.width(7)) comparator_7 (.a(instruction[6:0]), .b(7'b1100111), .eq(comparator_7_eq));  // open: gt, lt
  Comparator #(.width(7)) comparator_8 (.a(instruction[6:0]), .b(7'b1101111), .eq(comparator_8_eq));  // open: gt, lt
  Multiplexer #(.width(2), .enable("false")) multiplexer_2 (
    .in0(2'b00), .in1(2'b10), .out(multiplexer_2_out), .sel(comparator_9_eq));
  Comparator #(.width(7)) comparator_9 (.a(instruction[6:0]), .b(7'b0110111), .eq(comparator_9_eq));  // open: gt, lt
  Comparator #(.width(7)) comparator_10 (.a(instruction[6:0]), .b(7'b1100011), .eq(comparator_10_eq));  // open: gt, lt
  Comparator #(.width(7)) comparator_11 (.a(instruction[6:0]), .b(7'b1101111), .eq(comparator_11_eq));  // open: gt, lt
  Comparator #(.width(7)) comparator_12 (.a(instruction[6:0]), .b(7'b0110011), .eq(comparator_12_eq));  // open: gt, lt
  or or_2 (PCSel, and_5_out, comparator_7_eq, comparator_8_eq);
  or or_3 (ASel_PC, comparator_10_eq, comparator_11_eq);
  not not_2 (BSel, comparator_12_eq);
  Multiplexer #(.width(2), .enable("false")) multiplexer_3 (
    .in0(multiplexer_2_out), .in1(2'b01), .out(ASel), .sel(ASel_PC));
  Comparator #(.width(7)) comparator_13 (.a(instruction[6:0]), .b(7'b0100011), .eq(comparator_13_eq));  // open: gt, lt
  Comparator #(.width(7)) comparator_14 (.a(instruction[6:0]), .b(7'b1100011), .eq(comparator_14_eq));  // open: gt, lt
  Comparator #(.width(7)) comparator_15 (.a(instruction[6:0]), .b(7'b0110011), .eq(comparator_15_eq));  // open: gt, lt
  Comparator #(.width(7)) comparator_16 (.a(instruction[6:0]), .b(7'b0010011), .eq(comparator_16_eq));  // open: gt, lt
  or or_4 (or_4_out, comparator_13_eq, comparator_14_eq);
  or or_5 (or_5_out, comparator_15_eq, comparator_16_eq);
  Multiplexer #(.select(5), .width(4), .enable("false")) multiplexer_4 (
    .in0(4'b0000), .in1(4'b1010), .in2(4'b1100), .in4(4'b0110), .in5(4'b1110), .in8(4'b0111), .in13(4'b1011),
    .in16(4'b0011), .in20(4'b0100), .in21(4'b1000), .in24(4'b0010), .in28(4'b0001), .in29(4'b1001),
    .out(R_ALU), .sel({instruction[14:12], instruction[30], instruction[25]}));  // open: in3, in6, in7, in9, in10, in11, in12, in14, in15, in17, in18, in19, in22, in23, in25, in26, in27, in30, in31
  not not_3 (RegWEn, or_4_out);
  Multiplexer #(.select(5), .width(2), .enable("false")) multiplexer_5 (
    .in0(2'b10), .in4(2'b00), .in12(2'b00), .in13(2'b00), .in25(2'b01), .in27(2'b01), .out(WBSel),
    .sel(instruction[6:2]));  // open: in1, in2, in3, in5, in6, in7, in8, in9, in10, in11, in14, in15, in16, in17, in18, in19, in20, in21, in22, in23, in24, in26, in28, in29, in30, in31
  Multiplexer #(.width(4), .enable("false")) multiplexer_6 (.in0(4'b0000), .in1(funct), .out(ALUSel), .sel(or_5_out));
  Multiplexer #(.width(4), .enable("false")) multiplexer_7 (
    .in0(I_ALU), .in1(R_ALU), .out(funct), .sel(instruction[5]));
  Multiplexer #(.width(4), .enable("false")) multiplexer_8 (
    .in0(4'b0100), .in1(4'b0101), .out(multiplexer_8_out), .sel(instruction[30]));
  Multiplexer #(.select(3), .width(4), .enable("false")) multiplexer_9 (
    .in0(4'b0000), .in1(4'b0110), .in2(4'b0111), .in4(4'b0011), .in5(multiplexer_8_out), .in6(4'b0010),
    .in7(4'b0001), .out(I_ALU), .sel(instruction[14:12]));  // open: in3

  assign BrUn = instruction[13];

  // Other names for the same wires on the sheet: funct7[6:0] = instruction[31:25]; funct3[2:0] = instruction[14:12];
  //   Opcode[6:0] = instruction[6:0]

  // Notes on the sheet:
  //   Input
  //   output
  //   ImmSel
  //   PCSel
  //   BrUn
  //   A/BSel
  //   WBSel
endmodule
