// Logisim project cpu.circ as structural Verilog: 2 circuits, main circuit main
module main (
  input  [31:0] INSTRUCTION,
  input  CLOCK,
  output [31:0] PROGRAM_COUNTER,
  output [31:0] ra,
  output [31:0] sp,
  output [31:0] t0,
  output [31:0] t1,
  output [31:0] t2,
  output [31:0] s0,
  output [31:0] s1,
  output [31:0] a0
);

  wire DMEM_p1, DMEM_p3;
  wire [31:0] adder_1_out, ALU_res, Imm, INSTRUCTION_EX, Mem, RegFile_read_data_1, wb;

  Adder #(.width(32)) adder_1 (.a(PROGRAM_COUNTER), .b(32'h4), .out(adder_1_out));  // open: cin, cout
  Register #(.width(32)) PC (.D(adder_1_out), .clk(CLOCK), .Q(PROGRAM_COUNTER));  // open: en, clr
  ImmGen immgen_1 (.in_1(INSTRUCTION_EX), .out_2(Imm));
  Register #(.width(32)) register_1 (.D(INSTRUCTION), .en(1'b1), .clk(CLOCK), .Q(INSTRUCTION_EX));  // open: clr
  regfile_main RegFile (
    .rd(INSTRUCTION_EX[11:7]), .Read_Data_1(RegFile_read_data_1), .ra(ra), .sp(sp), .t0(t0), .t1(t1),
    .t2(t2), .s0(s0), .s1(s1), .a0(a0), .rs1(INSTRUCTION_EX[19:15]), .Write_Data(wb), .RegWEn(1'b1),
    .clk(CLOCK));  // open: rs2, Read_Data_2
  alu Arithmetic_Logic_Unit (.ALUSel(4'b0000), .B(Imm), .A(RegFile_read_data_1), .Result(ALU_res));
  // mem_main DMEM: pin names not known; wires that end beside it: DMEM_p1, DMEM_p1, DMEM_p3, Mem
  Multiplexer #(.width(32), .enable("false")) multiplexer_1 (.in0(ALU_res), .in1(Mem), .out(wb), .sel(1'b0));

  // Other names for the same wires on the sheet: clk = CLOCK; rd[4:0] = INSTRUCTION_EX[11:7];
  //   rs1[4:0] = INSTRUCTION_EX[19:15]

  // Notes on the sheet:
  //   Output
  //   IMEM (do **NOT** move this)
  //   Inputs
  //   It is OK to move the PC, RegFile, ALU, and MEM to wherever is most convenient for you when constructing your CPU, and to delete this text
  //   Inputs/Outputs for testing. Do **NOT** move these.
endmodule

module ImmGen (
  input  [31:0] in_1,
  output [31:0] out_2
);

  assign out_2 = {{20{in_1[31]}}, in_1[31:20]};  // Bit_Extender bit_extender_1

  // Other names for the same wires on the sheet: Imm[31:0] = out_2; instruction[31:0] = in_1
endmodule
